// Logisim project 32bitALU.circ as structural Verilog: 7 circuits, main circuit Logic Unit
module Logic_Unit (
  input  [1:0] OPCODE,
  input  [31:0] A,
  input  [31:0] B,
  output [31:0] OUTPUT
);

  wire [31:0] and_1_out, nor_1_out, or_1_out, xor_1_out;

  assign and_1_out = A & B;  // AND_Gate and_1, 32 bits wide
  assign or_1_out = A | B;  // OR_Gate or_1, 32 bits wide
  assign nor_1_out = ~(A | B);  // NOR_Gate nor_1, 32 bits wide
  assign xor_1_out = A ^ B;  // XOR_Gate xor_1, 32 bits wide
  Multiplexer #(.select(2), .width(32)) multiplexer_1 (
    .in0(and_1_out), .in1(or_1_out), .in2(nor_1_out), .in3(xor_1_out), .out(OUTPUT), .sel(OPCODE));  // open: en
endmodule

module Shifter (
  input  [31:0] A_LSB_5,
  input  [31:0] B,
  input  [1:0] OPCODE,
  output [31:0] OUTPUT
);

  wire [31:0] shifter_1_out, shifter_2_out, shifter_3_out;

  Shifter_part #(.width(32)) shifter_1 (.in(B), .\dist (A_LSB_5[4:0]), .out(shifter_1_out));
  Shifter_part #(.width(32), .shift("lr")) shifter_2 (.in(B), .\dist (A_LSB_5[4:0]), .out(shifter_2_out));
  Shifter_part #(.width(32), .shift("ar")) shifter_3 (.in(B), .\dist (A_LSB_5[4:0]), .out(shifter_3_out));
  Multiplexer #(.select(2), .width(32)) multiplexer_1 (
    .in0(B), .in1(shifter_1_out), .in2(shifter_2_out), .in3(shifter_3_out), .out(OUTPUT), .sel(OPCODE));  // open: en
endmodule

module Main_ALU (
  input  [1:0] OPCODE,
  input  [31:0] A,
  input  ADDER_OPCODE,
  input  [1:0] OPERATION_OPCODE,
  input  [31:0] B,
  output [31:0] out_6
);

  wire comparator_1_output;
  wire [31:0] adder_1_output, bit_extender_1_out, logic_unit_1_output, nor_1_out, shifter_1_output;

  Shifter shifter_1 (.A_LSB_5(A), .B(B), .OPCODE(OPCODE), .OUTPUT(shifter_1_output));
  Logic_Unit logic_unit_1 (.A(A), .B(B), .OPCODE(OPCODE), .OUTPUT(logic_unit_1_output));
  Comparator comparator_1 (.A(A), .B(B), .OUTPUT(comparator_1_output));
  Adder adder_1 (.A(A), .B(B), .OPCODE(ADDER_OPCODE), .OUTPUT(adder_1_output));
  assign bit_extender_1_out = {{31{1'b0}}, comparator_1_output};  // Bit_Extender bit_extender_1
  Multiplexer #(.select(2), .width(32)) multiplexer_1 (
    .in0(shifter_1_output), .in1(bit_extender_1_out), .in2(adder_1_output), .in3(logic_unit_1_output),
    .out(out_6), .sel(OPERATION_OPCODE));  // open: en
  assign nor_1_out = ~out_6;  // NOR_Gate nor_1, 32 bits wide NOR_Gate

  // Notes on the sheet:
  //   Comparator
  //   Adder
  //   Shifter Operation
  //   Logical Operation Unit
endmodule

module Comparator (
  input  [31:0] A,
  input  [31:0] B,
  output OUTPUT
);

  Comparator_part #(.width(32), .mode("unsigned")) comparator_1 (.a(A), .b(B), .lt(OUTPUT));  // open: gt, eq
endmodule

module Adder (
  input  [31:0] A,
  input  [31:0] B,
  input  OPCODE,
  output [31:0] OUTPUT
);

  wire [31:0] adder_1_out, subtractor_1_out;

  Adder_part #(.width(32)) adder_1 (.a(A), .b(B), .out(adder_1_out));  // open: cin, cout
  Multiplexer #(.width(32)) multiplexer_1 (
    .in0(adder_1_out), .in1(subtractor_1_out), .out(OUTPUT), .sel(OPCODE));  // open: en
  Subtractor #(.width(32)) subtractor_1 (.a(A), .b(B), .out(subtractor_1_out));  // open: bin, bout
endmodule

module _32_bit_Register_File (
  input  [4:0] RA,
  input  [4:0] RB,
  input  [31:0] BusW,
  input  [4:0] RW,
  input  RegWrite,
  output [31:0] BusA,
  output [31:0] BusB
);

  wire Clock_out, decoder_1_out0, decoder_1_out1, decoder_1_out2, decoder_1_out3, decoder_1_out4,
       decoder_1_out5, decoder_1_out6, decoder_1_out7, decoder_1_out8, decoder_1_out9, decoder_1_out10,
       decoder_1_out11, decoder_1_out12, decoder_1_out13, decoder_1_out14, decoder_1_out15, decoder_1_out16,
       decoder_1_out17, decoder_1_out18, decoder_1_out19, decoder_1_out20, decoder_1_out21, decoder_1_out22,
       decoder_1_out23, decoder_1_out24, decoder_1_out25, decoder_1_out26, decoder_1_out27, decoder_1_out28,
       decoder_1_out29, decoder_1_out30, decoder_1_out31, undriven, undriven_2, undriven_3, undriven_4,
       undriven_5, undriven_6, undriven_7, undriven_8, undriven_9, undriven_10, undriven_11, undriven_12,
       undriven_13, undriven_14, undriven_15, undriven_16, undriven_17, undriven_18, undriven_19,
       undriven_20, undriven_21, undriven_22, undriven_23, undriven_24, undriven_25, undriven_26,
       undriven_27, undriven_28, undriven_29, undriven_30, undriven_31, undriven_32;
  wire [31:0] register_1_q, register_2_q, register_3_q, register_4_q, register_5_q, register_6_q,
       register_7_q, register_8_q, register_9_q, register_10_q, register_11_q, register_12_q, register_13_q,
       register_14_q, register_15_q, register_16_q, register_17_q, register_18_q, register_19_q,
       register_20_q, register_21_q, register_22_q, register_23_q, register_24_q, register_25_q,
       register_26_q, register_27_q, register_28_q, register_29_q, register_30_q, register_31_q,
       register_32_q;

  Multiplexer #(.select(5), .width(32)) multiplexer_1 (
    .in0(register_1_q), .in1(register_2_q), .in2(register_3_q), .in3(register_4_q), .in4(register_5_q),
    .in5(register_6_q), .in6(register_7_q), .in7(register_8_q), .in8(register_9_q), .in9(register_10_q),
    .in10(register_11_q), .in11(register_12_q), .in12(register_13_q), .in13(register_14_q),
    .in14(register_15_q), .in15(register_16_q), .in16(register_17_q), .in17(register_18_q),
    .in18(register_19_q), .in19(register_20_q), .in20(register_21_q), .in21(register_22_q),
    .in22(register_23_q), .in23(register_24_q), .in24(register_25_q), .in25(register_26_q),
    .in26(register_27_q), .in27(register_28_q), .in28(register_29_q), .in29(register_30_q),
    .in30(register_31_q), .in31(register_32_q));  // open: out, sel, en
  Register #(.width(32)) register_1 (.D(BusW), .en(undriven_10), .Q(register_1_q), .clk(Clock_out));  // open: clr
  Register #(.width(32)) register_2 (.D(BusW), .en(undriven_3), .Q(register_2_q), .clk(Clock_out));  // open: clr
  Register #(.width(32)) register_3 (.D(BusW), .en(undriven_6), .Q(register_3_q), .clk(Clock_out));  // open: clr
  Register #(.width(32)) register_4 (.D(BusW), .en(undriven_11), .Q(register_4_q), .clk(Clock_out));  // open: clr
  // AND_Gate and_1 has open pins: in0=RegWrite, in1=decoder_1_out0, out=open
  // AND_Gate and_2 has open pins: in0=RegWrite, in1=decoder_1_out1, out=open
  // AND_Gate and_3 has open pins: in0=RegWrite, in1=decoder_1_out2, out=open
  // AND_Gate and_4 has open pins: in0=RegWrite, in1=decoder_1_out3, out=open
  // AND_Gate and_5 has open pins: in0=RegWrite, in1=decoder_1_out4, out=open
  // AND_Gate and_6 has open pins: in0=RegWrite, in1=decoder_1_out5, out=open
  // AND_Gate and_7 has open pins: in0=RegWrite, in1=decoder_1_out6, out=open
  // AND_Gate and_8 has open pins: in0=RegWrite, in1=decoder_1_out7, out=open
  // AND_Gate and_9 has open pins: in0=RegWrite, in1=decoder_1_out8, out=open
  // AND_Gate and_10 has open pins: in0=RegWrite, in1=decoder_1_out9, out=open
  // AND_Gate and_11 has open pins: in0=RegWrite, in1=decoder_1_out10, out=open
  // AND_Gate and_12 has open pins: in0=RegWrite, in1=decoder_1_out11, out=open
  // AND_Gate and_13 has open pins: in0=RegWrite, in1=decoder_1_out12, out=open
  // AND_Gate and_14 has open pins: in0=RegWrite, in1=decoder_1_out13, out=open
  // AND_Gate and_15 has open pins: in0=RegWrite, in1=decoder_1_out14, out=open
  // AND_Gate and_16 has open pins: in0=RegWrite, in1=decoder_1_out15, out=open
  Register #(.width(32)) register_5 (.D(BusW), .en(undriven), .Q(register_5_q), .clk(Clock_out));  // open: clr
  Register #(.width(32)) register_6 (.D(BusW), .en(undriven_12), .Q(register_6_q), .clk(Clock_out));  // open: clr
  Register #(.width(32)) register_7 (.D(BusW), .en(undriven_7), .Q(register_7_q), .clk(Clock_out));  // open: clr
  Register #(.width(32)) register_8 (.D(BusW), .en(undriven_13), .Q(register_8_q), .clk(Clock_out));  // open: clr
  Decoder #(.select(5)) decoder_1 (
    .out0(decoder_1_out0), .out1(decoder_1_out1), .out2(decoder_1_out2), .out3(decoder_1_out3),
    .out4(decoder_1_out4), .out5(decoder_1_out5), .out6(decoder_1_out6), .out7(decoder_1_out7),
    .out8(decoder_1_out8), .out9(decoder_1_out9), .out10(decoder_1_out10), .out11(decoder_1_out11),
    .out12(decoder_1_out12), .out13(decoder_1_out13), .out14(decoder_1_out14), .out15(decoder_1_out15),
    .out16(decoder_1_out16), .out17(decoder_1_out17), .out18(decoder_1_out18), .out19(decoder_1_out19),
    .out20(decoder_1_out20), .out21(decoder_1_out21), .out22(decoder_1_out22), .out23(decoder_1_out23),
    .out24(decoder_1_out24), .out25(decoder_1_out25), .out26(decoder_1_out26), .out27(decoder_1_out27),
    .out28(decoder_1_out28), .out29(decoder_1_out29), .out30(decoder_1_out30), .out31(decoder_1_out31));  // open: sel, en
  Register #(.width(32)) register_9 (.D(BusW), .en(undriven_2), .Q(register_9_q), .clk(Clock_out));  // open: clr
  Register #(.width(32)) register_10 (.D(BusW), .en(undriven_4), .Q(register_10_q), .clk(Clock_out));  // open: clr
  Register #(.width(32)) register_11 (.D(BusW), .en(undriven_14), .Q(register_11_q), .clk(Clock_out));  // open: clr
  Register #(.width(32)) register_12 (.D(BusW), .en(undriven_8), .Q(register_12_q), .clk(Clock_out));  // open: clr
  Register #(.width(32)) register_13 (.D(BusW), .en(undriven_15), .Q(register_13_q), .clk(Clock_out));  // open: clr
  Register #(.width(32)) register_14 (.D(BusW), .en(undriven_5), .Q(register_14_q), .clk(Clock_out));  // open: clr
  Register #(.width(32)) register_15 (.D(BusW), .en(undriven_16), .Q(register_15_q), .clk(Clock_out));  // open: clr
  Register #(.width(32)) register_16 (.D(BusW), .en(undriven_9), .Q(register_16_q), .clk(Clock_out));  // open: clr
  Register #(.width(32)) register_17 (.D(BusW), .en(undriven_17), .Q(register_17_q), .clk(Clock_out));  // open: clr
  Register #(.width(32)) register_18 (.D(BusW), .en(undriven_18), .Q(register_18_q), .clk(Clock_out));  // open: clr
  Register #(.width(32)) register_19 (.D(BusW), .en(undriven_19), .Q(register_19_q), .clk(Clock_out));  // open: clr
  Register #(.width(32)) register_20 (.D(BusW), .en(undriven_20), .Q(register_20_q), .clk(Clock_out));  // open: clr
  Register #(.width(32)) register_21 (.D(BusW), .en(undriven_21), .Q(register_21_q), .clk(Clock_out));  // open: clr
  Register #(.width(32)) register_22 (.D(BusW), .en(undriven_22), .Q(register_22_q), .clk(Clock_out));  // open: clr
  Register #(.width(32)) register_23 (.D(BusW), .en(undriven_23), .Q(register_23_q), .clk(Clock_out));  // open: clr
  Register #(.width(32)) register_24 (.D(BusW), .en(undriven_24), .Q(register_24_q), .clk(Clock_out));  // open: clr
  Register #(.width(32)) register_25 (.D(BusW), .en(undriven_25), .Q(register_25_q), .clk(Clock_out));  // open: clr
  Register #(.width(32)) register_26 (.D(BusW), .en(undriven_26), .Q(register_26_q), .clk(Clock_out));  // open: clr
  Register #(.width(32)) register_27 (.D(BusW), .en(undriven_27), .Q(register_27_q), .clk(Clock_out));  // open: clr
  Register #(.width(32)) register_28 (.D(BusW), .en(undriven_28), .Q(register_28_q), .clk(Clock_out));  // open: clr
  // AND_Gate and_17 has open pins: in0=RegWrite, in1=decoder_1_out31, out=open
  // AND_Gate and_18 has open pins: in0=RegWrite, in1=decoder_1_out30, out=open
  // AND_Gate and_19 has open pins: in0=RegWrite, in1=decoder_1_out29, out=open
  // AND_Gate and_20 has open pins: in0=RegWrite, in1=decoder_1_out28, out=open
  // AND_Gate and_21 has open pins: in0=RegWrite, in1=decoder_1_out27, out=open
  // AND_Gate and_22 has open pins: in0=RegWrite, in1=decoder_1_out26, out=open
  // AND_Gate and_23 has open pins: in0=RegWrite, in1=decoder_1_out25, out=open
  // AND_Gate and_24 has open pins: in0=RegWrite, in1=decoder_1_out24, out=open
  // AND_Gate and_25 has open pins: in0=RegWrite, in1=decoder_1_out23, out=open
  // AND_Gate and_26 has open pins: in0=RegWrite, in1=decoder_1_out22, out=open
  // AND_Gate and_27 has open pins: in0=RegWrite, in1=decoder_1_out21, out=open
  // AND_Gate and_28 has open pins: in0=RegWrite, in1=decoder_1_out20, out=open
  // AND_Gate and_29 has open pins: in0=RegWrite, in1=decoder_1_out19, out=open
  // AND_Gate and_30 has open pins: in0=RegWrite, in1=decoder_1_out18, out=open
  // AND_Gate and_31 has open pins: in0=RegWrite, in1=decoder_1_out17, out=open
  // AND_Gate and_32 has open pins: in0=RegWrite, in1=decoder_1_out16, out=open
  Register #(.width(32)) register_29 (.D(BusW), .en(undriven_29), .Q(register_29_q), .clk(Clock_out));  // open: clr
  Register #(.width(32)) register_30 (.D(BusW), .en(undriven_30), .Q(register_30_q), .clk(Clock_out));  // open: clr
  Register #(.width(32)) register_31 (.D(BusW), .en(undriven_31), .Q(register_31_q), .clk(Clock_out));  // open: clr
  Register #(.width(32)) register_32 (.D(BusW), .en(undriven_32), .Q(register_32_q), .clk(Clock_out));  // open: clr
  Multiplexer #(.select(5), .width(32)) multiplexer_2 (
    .in0(register_1_q), .in1(register_2_q), .in2(register_3_q), .in3(register_4_q), .in4(register_5_q),
    .in5(register_6_q), .in6(register_7_q), .in7(register_8_q), .in8(register_9_q), .in9(register_10_q),
    .in10(register_11_q), .in11(register_12_q), .in12(register_13_q), .in13(register_14_q),
    .in14(register_15_q), .in15(register_16_q), .in16(register_17_q), .in17(register_18_q),
    .in18(register_19_q), .in19(register_20_q), .in20(register_21_q), .in21(register_22_q),
    .in22(register_23_q), .in23(register_24_q), .in24(register_25_q), .in25(register_26_q),
    .in26(register_27_q), .in27(register_28_q), .in28(register_29_q), .in29(register_30_q),
    .in30(register_31_q), .in31(register_32_q));  // open: out, sel, en
  Clock Clock (.out(Clock_out));

  // Notes on the sheet:
  //   Least SIgnificant Register
  //   Most Significant Register
endmodule

module Memory (
  input  [23:0] in_1,
  input  [31:0] in_2,
  input  in_3,
  input  in_4,
  input  in_5,
  input  in_6,
  output [31:0] out_7
);

  wire clock_1_out;

  Clock clock_1 (.out(clock_1_out));
  RAM #(.addrWidth(24), .dataWidth(32), .bus("separate")) ram_1 (
    .addr(in_1), .din(in_2), .data(out_7), .str(in_3), .sel(in_4), .clk(clock_1_out), .ld(in_5), .clr(in_6));
endmodule
