// Logisim project File with working 32 bit Register.circ as structural Verilog: 15 circuits, main circuit Logic Unit
module Logic_Unit (
  input  [1:0] OPCODE,
  input  [31:0] A,
  input  [31:0] B,
  output [31:0] OUTPUT
);

  wire [31:0] and_1_out, nor_1_out, or_1_out, xor_1_out;

  assign and_1_out = A & B;  // AND_Gate and_1, 32 bits wide
  assign or_1_out = A | B;  // OR_Gate or_1, 32 bits wide
  assign nor_1_out = ~(A | B);  // NOR_Gate nor_1, 32 bits wide
  assign xor_1_out = A ^ B;  // XOR_Gate xor_1, 32 bits wide
  Multiplexer #(.select(2), .width(32)) multiplexer_1 (
    .in0(and_1_out), .in1(or_1_out), .in2(nor_1_out), .in3(xor_1_out), .out(OUTPUT), .sel(OPCODE));  // open: en
endmodule

module Shifter (
  input  [31:0] A_LSB_5,
  input  [31:0] B,
  input  [1:0] OPCODE,
  output [31:0] OUTPUT
);

  wire [31:0] shifter_1_out, shifter_2_out, shifter_3_out;

  Shifter_part #(.width(32)) shifter_1 (.in(B), .\dist (A_LSB_5[4:0]), .out(shifter_1_out));
  Shifter_part #(.width(32), .shift("lr")) shifter_2 (.in(B), .\dist (A_LSB_5[4:0]), .out(shifter_2_out));
  Shifter_part #(.width(32), .shift("ar")) shifter_3 (.in(B), .\dist (A_LSB_5[4:0]), .out(shifter_3_out));
  Multiplexer #(.select(2), .width(32)) multiplexer_1 (
    .in0(B), .in1(shifter_1_out), .in2(shifter_2_out), .in3(shifter_3_out), .out(OUTPUT), .sel(OPCODE));  // open: en
endmodule

module Main_ALU (
  input  [1:0] Shift_Logic_Opcode,
  input  [31:0] A,
  input  ADDER_OPCODE,
  input  [1:0] ALU_Opcode,
  input  [31:0] B,
  output [31:0] ALU_Output,
  output ZERO
);

  wire comparator_1_output;
  wire [31:0] adder_1_output, bit_extender_1_out, logic_unit_1_output, shifter_1_output;

  Shifter shifter_1 (.A_LSB_5(A), .B(B), .OPCODE(Shift_Logic_Opcode), .OUTPUT(shifter_1_output));
  Logic_Unit logic_unit_1 (.A(A), .B(B), .OPCODE(Shift_Logic_Opcode), .OUTPUT(logic_unit_1_output));
  Comparator comparator_1 (.A(A), .B(B), .OUTPUT(comparator_1_output));
  Adder adder_1 (.A(A), .B(B), .OPCODE(ADDER_OPCODE), .OUTPUT(adder_1_output));
  assign bit_extender_1_out = {{31{1'b0}}, comparator_1_output};  // Bit_Extender bit_extender_1
  Multiplexer #(.select(2), .width(32)) multiplexer_1 (
    .in0(shifter_1_output), .in1(bit_extender_1_out), .in2(adder_1_output), .in3(logic_unit_1_output),
    .out(ALU_Output), .sel(ALU_Opcode));  // open: en
  nor nor_1 (ZERO, ALU_Output[31], ALU_Output[30], ALU_Output[29], ALU_Output[28], ALU_Output[27], ALU_Output[26], ALU_Output[25], ALU_Output[24], ALU_Output[23], ALU_Output[22], ALU_Output[21], ALU_Output[20], ALU_Output[19], ALU_Output[18], ALU_Output[17], ALU_Output[16], ALU_Output[14], ALU_Output[13], ALU_Output[12], ALU_Output[11], ALU_Output[10], ALU_Output[9], ALU_Output[8], ALU_Output[7], ALU_Output[6], ALU_Output[5], ALU_Output[4], ALU_Output[3], ALU_Output[2], ALU_Output[1], ALU_Output[0], ALU_Output[15]);

  // Notes on the sheet:
  //   Comparator
  //   Adder
  //   Shifter Operation
  //   Logical Operation Unit
endmodule

module Comparator (
  input  [31:0] A,
  input  [31:0] B,
  output OUTPUT
);

  Comparator_part #(.width(32), .mode("unsigned")) comparator_1 (.a(A), .b(B), .lt(OUTPUT));  // open: gt, eq
endmodule

module Adder (
  input  [31:0] A,
  input  [31:0] B,
  input  OPCODE,
  output [31:0] OUTPUT
);

  wire [31:0] adder_1_out, subtractor_1_out;

  Adder_part #(.width(32)) adder_1 (.a(A), .b(B), .out(adder_1_out));  // open: cin, cout
  Multiplexer #(.width(32)) multiplexer_1 (
    .in0(adder_1_out), .in1(subtractor_1_out), .out(OUTPUT), .sel(OPCODE));  // open: en
  Subtractor #(.width(32)) subtractor_1 (.a(A), .b(B), .out(subtractor_1_out));  // open: bin, bout
endmodule

module _32_bit_Register_File (
  input  [4:0] RA,
  input  [4:0] RB,
  input  [4:0] WB,
  input  Clock,
  input  RegWrite,
  input  [31:0] BusW,
  output [31:0] BusA,
  output [31:0] BusB
);

  wire and_1_out, and_2_out, and_3_out, and_4_out, and_5_out, and_6_out, and_7_out, and_8_out, and_9_out,
       and_10_out, and_11_out, and_12_out, and_13_out, and_14_out, and_15_out, and_16_out, and_17_out,
       and_18_out, and_19_out, and_20_out, and_21_out, and_22_out, and_23_out, and_24_out, and_25_out,
       and_26_out, and_27_out, and_28_out, and_29_out, and_30_out, and_31_out, decoder_1_out1,
       decoder_1_out2, decoder_1_out3, decoder_1_out4, decoder_1_out5, decoder_1_out6, decoder_1_out7,
       decoder_1_out8, decoder_1_out9, decoder_1_out10, decoder_1_out11, decoder_1_out12, decoder_1_out13,
       decoder_1_out14, decoder_1_out15, decoder_1_out16, decoder_1_out17, decoder_1_out18, decoder_1_out19,
       decoder_1_out20, decoder_1_out21, decoder_1_out22, decoder_1_out23, decoder_1_out24, decoder_1_out25,
       decoder_1_out26, decoder_1_out27, decoder_1_out28, decoder_1_out29, decoder_1_out30, decoder_1_out31;
  wire [31:0] register_1_q, register_2_q, register_3_q, register_4_q, register_5_q, register_6_q,
       register_7_q, register_8_q, register_9_q, register_10_q, register_11_q, register_12_q, register_13_q,
       register_14_q, register_15_q, register_16_q, register_17_q, register_18_q, register_19_q,
       register_20_q, register_21_q, register_22_q, register_23_q, register_24_q, register_25_q,
       register_26_q, register_27_q, register_28_q, register_29_q, register_30_q, register_31_q,
       register_32_q;

  Multiplexer #(.select(5), .width(32)) multiplexer_1 (
    .in0(register_1_q), .in1(register_2_q), .in2(register_3_q), .in3(register_4_q), .in4(register_5_q),
    .in5(register_6_q), .in6(register_7_q), .in7(register_8_q), .in8(register_9_q), .in9(register_10_q),
    .in10(register_11_q), .in11(register_12_q), .in12(register_13_q), .in13(register_14_q),
    .in14(register_15_q), .in15(register_16_q), .in16(register_17_q), .in17(register_18_q),
    .in18(register_19_q), .in19(register_20_q), .in20(register_21_q), .in21(register_22_q),
    .in22(register_23_q), .in23(register_24_q), .in24(register_25_q), .in25(register_26_q),
    .in26(register_27_q), .in27(register_28_q), .in28(register_29_q), .in29(register_30_q),
    .in30(register_31_q), .in31(register_32_q), .out(BusA), .sel(RA));  // open: en
  Register #(.width(32)) register_1 (.Q(register_1_q));  // open: D, en, clk, clr
  Register #(.width(32)) register_2 (.D(BusW), .en(and_1_out), .Q(register_2_q), .clk(Clock));  // open: clr
  Register #(.width(32)) register_3 (.D(BusW), .en(and_2_out), .Q(register_3_q), .clk(Clock));  // open: clr
  Register #(.width(32)) register_4 (.D(BusW), .en(and_3_out), .Q(register_4_q), .clk(Clock));  // open: clr
  and and_1 (and_1_out, RegWrite, decoder_1_out1);
  and and_2 (and_2_out, RegWrite, decoder_1_out2);
  and and_3 (and_3_out, RegWrite, decoder_1_out3);
  and and_4 (and_4_out, RegWrite, decoder_1_out4);
  and and_5 (and_5_out, RegWrite, decoder_1_out5);
  and and_6 (and_6_out, RegWrite, decoder_1_out6);
  and and_7 (and_7_out, RegWrite, decoder_1_out7);
  and and_8 (and_8_out, RegWrite, decoder_1_out8);
  and and_9 (and_9_out, RegWrite, decoder_1_out9);
  and and_10 (and_10_out, RegWrite, decoder_1_out10);
  and and_11 (and_11_out, RegWrite, decoder_1_out11);
  and and_12 (and_12_out, RegWrite, decoder_1_out12);
  and and_13 (and_13_out, RegWrite, decoder_1_out13);
  and and_14 (and_14_out, RegWrite, decoder_1_out14);
  and and_15 (and_15_out, RegWrite, decoder_1_out15);
  Register #(.width(32)) register_5 (.D(BusW), .en(and_4_out), .Q(register_5_q), .clk(Clock));  // open: clr
  Register #(.width(32)) register_6 (.D(BusW), .en(and_5_out), .Q(register_6_q), .clk(Clock));  // open: clr
  Register #(.width(32)) register_7 (.D(BusW), .en(and_6_out), .Q(register_7_q), .clk(Clock));  // open: clr
  Register #(.width(32)) register_8 (.D(BusW), .en(and_7_out), .Q(register_8_q), .clk(Clock));  // open: clr
  Decoder #(.select(5)) decoder_1 (
    .out1(decoder_1_out1), .out2(decoder_1_out2), .out3(decoder_1_out3), .out4(decoder_1_out4),
    .out5(decoder_1_out5), .out6(decoder_1_out6), .out7(decoder_1_out7), .out8(decoder_1_out8),
    .out9(decoder_1_out9), .out10(decoder_1_out10), .out11(decoder_1_out11), .out12(decoder_1_out12),
    .out13(decoder_1_out13), .out14(decoder_1_out14), .out15(decoder_1_out15), .out16(decoder_1_out16),
    .out17(decoder_1_out17), .out18(decoder_1_out18), .out19(decoder_1_out19), .out20(decoder_1_out20),
    .out21(decoder_1_out21), .out22(decoder_1_out22), .out23(decoder_1_out23), .out24(decoder_1_out24),
    .out25(decoder_1_out25), .out26(decoder_1_out26), .out27(decoder_1_out27), .out28(decoder_1_out28),
    .out29(decoder_1_out29), .out30(decoder_1_out30), .out31(decoder_1_out31), .sel(WB));  // open: out0, en
  Register #(.width(32)) register_9 (.D(BusW), .en(and_8_out), .Q(register_9_q), .clk(Clock));  // open: clr
  Register #(.width(32)) register_10 (.D(BusW), .en(and_9_out), .Q(register_10_q), .clk(Clock));  // open: clr
  Register #(.width(32)) register_11 (.D(BusW), .en(and_10_out), .Q(register_11_q), .clk(Clock));  // open: clr
  Register #(.width(32)) register_12 (.D(BusW), .en(and_11_out), .Q(register_12_q), .clk(Clock));  // open: clr
  Register #(.width(32)) register_13 (.D(BusW), .en(and_12_out), .Q(register_13_q), .clk(Clock));  // open: clr
  Register #(.width(32)) register_14 (.D(BusW), .en(and_13_out), .Q(register_14_q), .clk(Clock));  // open: clr
  Register #(.width(32)) register_15 (.D(BusW), .en(and_14_out), .Q(register_15_q), .clk(Clock));  // open: clr
  Register #(.width(32)) register_16 (.D(BusW), .en(and_15_out), .Q(register_16_q), .clk(Clock));  // open: clr
  Register #(.width(32)) register_17 (.D(BusW), .en(and_31_out), .Q(register_17_q), .clk(Clock));  // open: clr
  Register #(.width(32)) register_18 (.D(BusW), .en(and_30_out), .Q(register_18_q), .clk(Clock));  // open: clr
  Register #(.width(32)) register_19 (.D(BusW), .en(and_29_out), .Q(register_19_q), .clk(Clock));  // open: clr
  Register #(.width(32)) register_20 (.D(BusW), .en(and_28_out), .Q(register_20_q), .clk(Clock));  // open: clr
  Register #(.width(32)) register_21 (.D(BusW), .en(and_27_out), .Q(register_21_q), .clk(Clock));  // open: clr
  Register #(.width(32)) register_22 (.D(BusW), .en(and_26_out), .Q(register_22_q), .clk(Clock));  // open: clr
  Register #(.width(32)) register_23 (.D(BusW), .en(and_25_out), .Q(register_23_q), .clk(Clock));  // open: clr
  Register #(.width(32)) register_24 (.D(BusW), .en(and_24_out), .Q(register_24_q), .clk(Clock));  // open: clr
  Register #(.width(32)) register_25 (.D(BusW), .en(and_23_out), .Q(register_25_q), .clk(Clock));  // open: clr
  Register #(.width(32)) register_26 (.D(BusW), .en(and_22_out), .Q(register_26_q), .clk(Clock));  // open: clr
  Register #(.width(32)) register_27 (.D(BusW), .en(and_21_out), .Q(register_27_q), .clk(Clock));  // open: clr
  Register #(.width(32)) register_28 (.D(BusW), .en(and_20_out), .Q(register_28_q), .clk(Clock));  // open: clr
  and and_16 (and_16_out, RegWrite, decoder_1_out31);
  and and_17 (and_17_out, RegWrite, decoder_1_out30);
  and and_18 (and_18_out, RegWrite, decoder_1_out29);
  and and_19 (and_19_out, RegWrite, decoder_1_out28);
  and and_20 (and_20_out, RegWrite, decoder_1_out27);
  and and_21 (and_21_out, RegWrite, decoder_1_out26);
  and and_22 (and_22_out, RegWrite, decoder_1_out25);
  and and_23 (and_23_out, RegWrite, decoder_1_out24);
  and and_24 (and_24_out, RegWrite, decoder_1_out23);
  and and_25 (and_25_out, RegWrite, decoder_1_out22);
  and and_26 (and_26_out, RegWrite, decoder_1_out21);
  and and_27 (and_27_out, RegWrite, decoder_1_out20);
  and and_28 (and_28_out, RegWrite, decoder_1_out19);
  and and_29 (and_29_out, RegWrite, decoder_1_out18);
  and and_30 (and_30_out, RegWrite, decoder_1_out17);
  and and_31 (and_31_out, RegWrite, decoder_1_out16);
  Register #(.width(32)) register_29 (.D(BusW), .en(and_19_out), .Q(register_29_q), .clk(Clock));  // open: clr
  Register #(.width(32)) register_30 (.D(BusW), .en(and_18_out), .Q(register_30_q), .clk(Clock));  // open: clr
  Register #(.width(32)) register_31 (.D(BusW), .en(and_17_out), .Q(register_31_q), .clk(Clock));  // open: clr
  Register #(.width(32)) register_32 (.D(BusW), .en(and_16_out), .Q(register_32_q), .clk(Clock));  // open: clr
  Multiplexer #(.select(5), .width(32)) multiplexer_2 (
    .in0(register_1_q), .in1(register_2_q), .in2(register_3_q), .in3(register_4_q), .in4(register_5_q),
    .in5(register_6_q), .in6(register_7_q), .in7(register_8_q), .in8(register_9_q), .in9(register_10_q),
    .in10(register_11_q), .in11(register_12_q), .in12(register_13_q), .in13(register_14_q),
    .in14(register_15_q), .in15(register_16_q), .in16(register_17_q), .in17(register_18_q),
    .in18(register_19_q), .in19(register_20_q), .in20(register_21_q), .in21(register_22_q),
    .in22(register_23_q), .in23(register_24_q), .in24(register_25_q), .in25(register_26_q),
    .in26(register_27_q), .in27(register_28_q), .in28(register_29_q), .in29(register_30_q),
    .in30(register_31_q), .in31(register_32_q), .out(BusB), .sel(RB));  // open: en

  // Notes on the sheet:
  //   Least SIgnificant Register
  //   Hard 0 register
  //   Most Significant Register
endmodule

module Chip (
  input  [23:0] Address,
  input  [7:0] Input,
  input  Store,
  input  Chip_enable,
  input  Clock,
  input  Load,
  input  Clear,
  output [7:0] Output
);

  RAM #(.addrWidth(24), .bus("separate")) ram_1 (
    .addr(Address), .din(Input), .data(Output), .str(Store), .sel(Chip_enable), .clk(Clock), .ld(Load),
    .clr(Clear));
endmodule

module Module (
  input  [23:0] Address,
  input  Store,
  input  Clock,
  input  Load,
  input  Clear,
  input  Module_enable,
  input  [1:0] Chip_select,
  input  [31:0] Input,
  input  [3:0] Load_Byte,
  input  [3:0] Load_Half,
  input  [3:0] Load_Word,
  output [31:0] Output
);

  wire and_1_out, and_2_out, and_3_out, and_4_out;
  wire [3:0] multiplexer_1_out;

  and and_1 (and_1_out, multiplexer_1_out[3], Module_enable);
  and and_2 (and_2_out, multiplexer_1_out[2], Module_enable);
  and and_3 (and_3_out, multiplexer_1_out[1], Module_enable);
  and and_4 (and_4_out, Module_enable, multiplexer_1_out[0]);
  Multiplexer #(.select(2), .width(4)) multiplexer_1 (
    .in0(Load_Byte), .in1(Load_Half), .in2(Load_Word), .out(multiplexer_1_out), .sel(Chip_select),
    .en(Module_enable));  // open: in3
  Chip Chip_3 (
    .Address(Address), .Input(Input[31:24]), .Store(Store), .Chip_enable(and_1_out), .Clock(Clock),
    .Load(Load), .Clear(Clear), .Output(Output[31:24]));
  Chip Chip_2 (
    .Address(Address), .Input(Input[23:16]), .Store(Store), .Chip_enable(and_2_out), .Clock(Clock),
    .Load(Load), .Clear(Clear), .Output(Output[23:16]));
  Chip Chip_1 (
    .Address(Address), .Input(Input[15:8]), .Store(Store), .Chip_enable(and_3_out), .Clock(Clock),
    .Load(Load), .Clear(Clear), .Output(Output[15:8]));
  Chip Chip_0 (
    .Address(Address), .Input(Input[7:0]), .Store(Store), .Chip_enable(and_4_out), .Clock(Clock),
    .Load(Load), .Clear(Clear), .Output(Output[7:0]));

  // Other names for the same wires on the sheet: Chip_0[7:0] = Input[7:0]; Chip_1[7:0] = Input[15:8];
  //   Chip_2[7:0] = Input[23:16]; Chip_3[7:0] = Input[31:24]
endmodule

module Bank (
  input  [3:0] Load_Word,
  input  [3:0] Load_Half,
  input  [3:0] Load_Byte,
  input  [23:0] Addres,
  input  [1:0] Chip_Select,
  input  Store,
  input  Clock,
  input  Load,
  input  Clear,
  input  [31:0] Input,
  input  [2:0] Select_Module,
  input  Bank_enable,
  output [31:0] Output
);

  wire decoder_1_out0, decoder_1_out1, decoder_1_out2, decoder_1_out3, decoder_1_out4, decoder_1_out5,
       decoder_1_out6, decoder_1_out7, Module_0, Module_1, Module_2, Module_3, Module_4, Module_5, Module_6,
       Module_7;
  wire [31:0] Module_0_output, Module_1_output, Module_2_output, Module_3_output, Module_4_output,
       Module_5_output, Module_6_output, Module_7_output;

  Module u_Module_7 (
    .Address(Addres), .Store(Store), .Clock(Clock), .Load(Load), .Clear(Clear), .Input(Input),
    .Load_Byte(Load_Byte), .Load_Half(Load_Half), .Load_Word(Load_Word), .Output(Module_7_output),
    .Module_enable(Module_7), .Chip_select(Chip_Select));
  Module u_Module_6 (
    .Address(Addres), .Store(Store), .Clock(Clock), .Load(Load), .Clear(Clear), .Input(Input),
    .Load_Byte(Load_Byte), .Load_Half(Load_Half), .Load_Word(Load_Word), .Output(Module_6_output),
    .Module_enable(Module_6), .Chip_select(Chip_Select));
  Module u_Module_5 (
    .Address(Addres), .Store(Store), .Clock(Clock), .Load(Load), .Clear(Clear), .Input(Input),
    .Load_Byte(Load_Byte), .Load_Half(Load_Half), .Load_Word(Load_Word), .Output(Module_5_output),
    .Module_enable(Module_5), .Chip_select(Chip_Select));
  Decoder #(.select(3)) decoder_1 (
    .out0(decoder_1_out0), .out1(decoder_1_out1), .out2(decoder_1_out2), .out3(decoder_1_out3),
    .out4(decoder_1_out4), .out5(decoder_1_out5), .out6(decoder_1_out6), .out7(decoder_1_out7),
    .sel(Select_Module), .en(Bank_enable));
  Module u_Module_4 (
    .Address(Addres), .Store(Store), .Clock(Clock), .Load(Load), .Clear(Clear), .Input(Input),
    .Load_Byte(Load_Byte), .Load_Half(Load_Half), .Load_Word(Load_Word), .Output(Module_4_output),
    .Module_enable(Module_4), .Chip_select(Chip_Select));
  Multiplexer #(.select(3), .width(32)) multiplexer_1 (
    .in0(Module_0_output), .in1(Module_1_output), .in2(Module_2_output), .in3(Module_3_output),
    .in4(Module_4_output), .in5(Module_5_output), .in6(Module_6_output), .in7(Module_7_output), .out(Output),
    .sel(Select_Module));  // open: en
  Module u_Module_3 (
    .Address(Addres), .Store(Store), .Clock(Clock), .Load(Load), .Clear(Clear), .Input(Input),
    .Load_Byte(Load_Byte), .Load_Half(Load_Half), .Load_Word(Load_Word), .Output(Module_3_output),
    .Module_enable(Module_3), .Chip_select(Chip_Select));
  and and_1 (Module_0, decoder_1_out0, Bank_enable);
  and and_2 (Module_1, decoder_1_out1, Bank_enable);
  and and_3 (Module_2, decoder_1_out2, Bank_enable);
  Module u_Module_2 (
    .Address(Addres), .Store(Store), .Clock(Clock), .Load(Load), .Clear(Clear), .Input(Input),
    .Load_Byte(Load_Byte), .Load_Half(Load_Half), .Load_Word(Load_Word), .Output(Module_2_output),
    .Module_enable(Module_2), .Chip_select(Chip_Select));
  and and_4 (Module_3, decoder_1_out3, Bank_enable);
  and and_5 (Module_4, decoder_1_out4, Bank_enable);
  and and_6 (Module_5, decoder_1_out5, Bank_enable);
  Module u_Module_1 (
    .Address(Addres), .Store(Store), .Clock(Clock), .Load(Load), .Clear(Clear), .Input(Input),
    .Load_Byte(Load_Byte), .Load_Half(Load_Half), .Load_Word(Load_Word), .Output(Module_1_output),
    .Module_enable(Module_1), .Chip_select(Chip_Select));
  and and_7 (Module_6, decoder_1_out6, Bank_enable);
  and and_8 (Module_7, decoder_1_out7, Bank_enable);
  Module u_Module_0 (
    .Address(Addres), .Store(Store), .Clock(Clock), .Load(Load), .Clear(Clear), .Input(Input),
    .Load_Byte(Load_Byte), .Load_Half(Load_Half), .Load_Word(Load_Word), .Output(Module_0_output),
    .Module_enable(Module_0), .Chip_select(Chip_Select));

  // Other names for the same wires on the sheet: address[23:0] = Addres
endmodule

module _4GB_RAM (
  input  [31:0] Input,
  input  [31:0] Address,
  input  Clear,
  input  Load,
  input  Clock,
  input  Store,
  input  [3:0] Load_Word,
  input  [3:0] Load_Half,
  input  [3:0] Load_Byte,
  output [31:0] Final_Output
);

  wire Bank_0, Bank_1, Bank_2, Bank_3, Bank_4, Bank_5, Bank_6, Bank_7;
  wire [31:0] OUTPUT_BANK_0, OUTPUT_BANK_1, OUTPUT_BANK_2, OUTPUT_BANK_3, OUTPUT_BANK_4, OUTPUT_BANK_5,
       OUTPUT_BANK_6, OUTPUT_BANK_7;

  Decoder #(.select(3)) decoder_1 (
    .out0(Bank_0), .out1(Bank_1), .out2(Bank_2), .out3(Bank_3), .out4(Bank_4), .out5(Bank_5), .out6(Bank_6),
    .out7(Bank_7), .sel(Address[31:29]));  // open: en
  Bank u_bank_1 (
    .Select_Module(Address[28:26]), .Bank_enable(Bank_0), .Addres(Address[25:2]), .Input(Input),
    .Store(Store), .Clock(Clock), .Load(Load), .Clear(Clear), .Chip_Select(Address[1:0]),
    .Load_Word(Load_Word), .Load_Half(Load_Half), .Load_Byte(Load_Byte), .Output(OUTPUT_BANK_0));
  Bank u_bank_2 (
    .Select_Module(Address[28:26]), .Bank_enable(Bank_1), .Addres(Address[25:2]), .Input(Input),
    .Store(Store), .Clock(Clock), .Load(Load), .Clear(Clear), .Chip_Select(Address[1:0]),
    .Load_Word(Load_Word), .Load_Half(Load_Half), .Load_Byte(Load_Byte), .Output(OUTPUT_BANK_1));
  Bank u_bank_3 (
    .Select_Module(Address[28:26]), .Bank_enable(Bank_2), .Addres(Address[25:2]), .Input(Input),
    .Store(Store), .Clock(Clock), .Load(Load), .Clear(Clear), .Chip_Select(Address[1:0]),
    .Load_Word(Load_Word), .Load_Half(Load_Half), .Load_Byte(Load_Byte), .Output(OUTPUT_BANK_2));
  Bank u_bank_4 (
    .Select_Module(Address[28:26]), .Bank_enable(Bank_3), .Addres(Address[25:2]), .Input(Input),
    .Store(Store), .Clock(Clock), .Load(Load), .Clear(Clear), .Chip_Select(Address[1:0]),
    .Load_Word(Load_Word), .Load_Half(Load_Half), .Load_Byte(Load_Byte), .Output(OUTPUT_BANK_3));
  Bank u_bank_5 (
    .Select_Module(Address[28:26]), .Bank_enable(Bank_4), .Addres(Address[25:2]), .Input(Input),
    .Store(Store), .Clock(Clock), .Load(Load), .Clear(Clear), .Chip_Select(Address[1:0]),
    .Load_Word(Load_Word), .Load_Half(Load_Half), .Load_Byte(Load_Byte), .Output(OUTPUT_BANK_4));
  Bank u_bank_6 (
    .Select_Module(Address[28:26]), .Bank_enable(Bank_5), .Addres(Address[25:2]), .Input(Input),
    .Store(Store), .Clock(Clock), .Load(Load), .Clear(Clear), .Chip_Select(Address[1:0]),
    .Load_Word(Load_Word), .Load_Half(Load_Half), .Load_Byte(Load_Byte), .Output(OUTPUT_BANK_5));
  Multiplexer #(.select(3), .width(32)) multiplexer_1 (
    .in0(OUTPUT_BANK_0), .in1(OUTPUT_BANK_1), .in2(OUTPUT_BANK_2), .in3(OUTPUT_BANK_3), .in4(OUTPUT_BANK_4),
    .in5(OUTPUT_BANK_5), .in6(OUTPUT_BANK_6), .in7(OUTPUT_BANK_7), .out(Final_Output), .sel(Address[31:29]));  // open: en
  Bank u_bank_7 (
    .Select_Module(Address[28:26]), .Bank_enable(Bank_6), .Addres(Address[25:2]), .Input(Input),
    .Store(Store), .Clock(Clock), .Load(Load), .Clear(Clear), .Chip_Select(Address[1:0]),
    .Load_Word(Load_Word), .Load_Half(Load_Half), .Load_Byte(Load_Byte), .Output(OUTPUT_BANK_6));
  Bank bank_8 (
    .Select_Module(Address[28:26]), .Bank_enable(Bank_7), .Addres(Address[25:2]), .Input(Input),
    .Store(Store), .Clock(Clock), .Load(Load), .Clear(Clear), .Chip_Select(Address[1:0]),
    .Load_Word(Load_Word), .Load_Half(Load_Half), .Load_Byte(Load_Byte), .Output(OUTPUT_BANK_7));

  // Other names for the same wires on the sheet: Select[1:0] = Address[1:0]; Address_t[23:0] = Address[25:2];
  //   Select_Module[2:0] = Address[28:26]
endmodule

module Single_Cycle_CPU (
  input  [1:0] in_1,
  input  RESET,
  input  in_3,
  input  in_4,
  input  Clear,
  input  [31:0] in_6,
  input  Load,
  input  Clock,
  input  Store,
  input  [3:0] Load_Word,
  input  [31:0] Input,
  input  in_12,
  input  [3:0] Load_Half,
  input  [1:0] in_14,
  input  [3:0] Load_Byte,
  input  [1:0] IGNORE_THIS_HARDCODED_TEMP,
  input  [31:0] BusW,
  output [31:0] out_18,
  output [31:0] Final_Output
);

  wire ALUOp0, ALUOp1, ALUOp2, ALUSrc, Clock_t, ExtOP, main_alu_1_p7, MemRd, MemtoReg, MemWr,
       pc_controller_1_pcsrc0, pc_controller_1_pcsrc1, PCCtrl0, PCCtrl1, RegDst, RegWr;
  wire [2:0] ALU_Opcode;
  wire [3:0] undriven;
  wire [4:0] multiplexer_2_out;
  wire [31:0] adder_1_out, adder_2_out, ALU_Result, Immediate_16_Extended, Immediate_26_Extendeed,
       Instruction_Address, multiplexer_1_out, Output_Register_BusA, Output_Register_BusB;

  Clock clock_1 (.out(Clock_t));
  Multiplexer #(.select(2), .width(32)) multiplexer_1 (
    .in0(adder_1_out), .in1(Immediate_26_Extendeed), .in2(adder_2_out), .out(multiplexer_1_out), .sel(in_1));  // open: in3, en
  Adder_part #(.width(32)) adder_1 (.a(32'h4), .b(Instruction_Address), .out(adder_1_out));  // open: cin, cout
  Register #(.width(32)) register_1 (
    .D(multiplexer_1_out), .Q(Instruction_Address), .clk(Clock_t), .clr(RESET));  // open: en
  ALU_Control alu_control_1 (
    .ALU_Control_Input(undriven), .ALUOp2(ALUOp2), .ALUOp1(ALUOp1), .ALUOp0(ALUOp0), .ALU_Opcode(ALU_Opcode));
  _4GB_RAM u_4gb_ram_1 (
    .Address(Instruction_Address), .Clear(in_3), .Load(1'b1), .Clock(Clock_t), .Store(in_4),
    .Load_Word(4'b1111), .Load_Half(4'b1111), .Load_Byte(4'b1111), .Final_Output(out_18), .Input(in_6));
  Adder_part #(.width(32)) adder_2 (.a(adder_1_out), .b(Immediate_16_Extended), .out(adder_2_out));  // open: cin, cout
  // Main_ALU main_alu_1: pin names not known; wires that end beside it: Output_Register_BusA, Output_Register_BusB, in_14, IGNORE_THIS_HARDCODED_TEMP, in_12, ALU_Result, main_alu_1_p7
  MainControl maincontrol_1 (
    .MainControl_Input(out_18[31:26]), .RegDst(RegDst), .RegWrite(RegWr), .ExtOp(ExtOP), .ALUSrc(ALUSrc),
    .MemRd(MemRd), .MemWr(MemWr), .MemtoReg(MemtoReg), .ALUOp2(ALUOp2), .ALUOp1(ALUOp1), .ALUOp0(ALUOp0),
    .PCCtrl1(PCCtrl1), .PCCtrl0(PCCtrl0));
  PC_Controller pc_controller_1 (
    .Zero(1'b0), .PCCtrl1(PCCtrl1), .PCCtrl0(PCCtrl0), .PCSrc1(pc_controller_1_pcsrc1),
    .PCSrc0(pc_controller_1_pcsrc0));
  Extender extender_1 (._16bit_Input(out_18[15:0]), .Select(ExtOP), .Output(Immediate_16_Extended));
  assign Immediate_26_Extendeed = {{6{1'b0}}, out_18[25:0]};  // Bit_Extender bit_extender_1
  Multiplexer #(.width(5)) multiplexer_2 (
    .in0(out_18[20:16]), .in1(out_18[15:11]), .out(multiplexer_2_out), .sel(RegDst));  // open: en
  _4GB_RAM u_4gb_ram_2 (
    .Address(ALU_Result), .Clear(Clear), .Load(Load), .Clock(Clock), .Store(Store), .Load_Word(Load_Word),
    .Load_Half(Load_Half), .Load_Byte(Load_Byte), .Final_Output(Final_Output), .Input(Input));
  _32_bit_Register_File u_32_bit_register_file_1 (
    .RA(out_18[25:21]), .RB(out_18[20:16]), .WB(multiplexer_2_out), .BusW(BusW), .RegWrite(RegWr),
    .Clock(Clock_t), .BusA(Output_Register_BusA), .BusB(Output_Register_BusB));

  // Other names for the same wires on the sheet: Funct[5:0] = out_18[5:0]; Immediate_16[15:0] = out_18[15:0];
  //   Immediate_26[25:0] = out_18[25:0]; Instruction[31:0] = out_18; R_2[4:0] = out_18[15:11];
  //   R_1[4:0] = out_18[20:16]; RA[4:0] = out_18[25:21]; Opcode[5:0] = out_18[31:26]; PCSrc[1:0] = in_1

  // Notes on the sheet:
  //   PROGRAM COUNTER
  //   INSTRUCTION REGISTER
  //   ALU
  //   PC Control
  //   ALU Control
  //   Main Control (Some not done yet like ExtOP)
  //   IF YOU WANT TO MANUALLY INPUT COMMANDS
  //   PC Controller
  //   Opcode Determines Everything
  //   For now we need to hardcode the operations
  //   set load word to 15, load half to 3, and load byte to 1
  //   so lw is 1111, lf 0011,lb, 0001
endmodule

module MainControl (
  input  [5:0] MainControl_Input,
  output RegDst,
  output RegWrite,
  output ExtOp,
  output ALUSrc,
  output MemRd,
  output MemWr,
  output MemtoReg,
  output ALUOp2,
  output ALUOp1,
  output ALUOp0,
  output PCCtrl1,
  output PCCtrl0
);

  wire ADDI_out, ANDI_out, BEQ_out, BNE_out, JUMP_out, ORI_out, XORI_out;

  and R_type (RegDst, ~MainControl_Input[5], ~MainControl_Input[4], ~MainControl_Input[3], ~MainControl_Input[2], ~MainControl_Input[1], ~MainControl_Input[0]);  // AND_Gate
  and LW (MemRd, MainControl_Input[5], ~MainControl_Input[4], ~MainControl_Input[3], ~MainControl_Input[2], MainControl_Input[1], MainControl_Input[0]);  // AND_Gate
  and SW (MemWr, MainControl_Input[5], ~MainControl_Input[4], MainControl_Input[3], ~MainControl_Input[2], MainControl_Input[1], MainControl_Input[0]);  // AND_Gate
  and BEQ (BEQ_out, ~MainControl_Input[5], ~MainControl_Input[4], ~MainControl_Input[3], MainControl_Input[2], ~MainControl_Input[1], ~MainControl_Input[0]);  // AND_Gate
  and BNE (BNE_out, ~MainControl_Input[5], ~MainControl_Input[4], ~MainControl_Input[3], MainControl_Input[2], ~MainControl_Input[1], MainControl_Input[0]);  // AND_Gate
  and ANDI (ANDI_out, ~MainControl_Input[5], ~MainControl_Input[4], MainControl_Input[3], MainControl_Input[2], MainControl_Input[1], MainControl_Input[0]);  // AND_Gate
  and ORI (ORI_out, ~MainControl_Input[5], ~MainControl_Input[4], MainControl_Input[3], MainControl_Input[2], ~MainControl_Input[1], MainControl_Input[0]);  // AND_Gate
  and XORI (XORI_out, ~MainControl_Input[5], ~MainControl_Input[4], MainControl_Input[3], MainControl_Input[2], MainControl_Input[1], ~MainControl_Input[0]);  // AND_Gate
  and ADDI (ADDI_out, ~MainControl_Input[5], ~MainControl_Input[4], MainControl_Input[3], ~MainControl_Input[2], ~MainControl_Input[1], ~MainControl_Input[0]);  // AND_Gate
  // AND_Gate SLTI has open pins: in0=MainControl_Input[5], in1=MainControl_Input[4], in2=MainControl_Input[3], in3=MainControl_Input[2], in4=MainControl_Input[1], in5=MainControl_Input[0], out=open
  and JUMP (JUMP_out, ~MainControl_Input[5], ~MainControl_Input[4], ~MainControl_Input[3], ~MainControl_Input[2], MainControl_Input[1], ~MainControl_Input[0]);  // AND_Gate
  nor nor_1 (RegWrite, MemWr, BEQ_out, BNE_out, JUMP_out);
  nor nor_2 (ExtOp, ANDI_out, ORI_out, XORI_out);
  nor nor_3 (ALUSrc, RegDst, BEQ_out, BNE_out);
  nor nor_4 (ALUOp2, RegDst, ANDI_out, ORI_out, XORI_out);
  or or_1 (ALUOp1, ORI_out, XORI_out);
  nor nor_5 (ALUOp0, RegDst, MemWr, MemRd, ORI_out, ADDI_out);
  or or_2 (PCCtrl1, BEQ_out, JUMP_out);
  or or_3 (PCCtrl0, BNE_out, JUMP_out);

  assign MemtoReg = MemRd;
endmodule

module Extender (
  input  [15:0] _16bit_Input,
  input  Select,
  output [31:0] Output
);

  wire [31:0] bit_extender_1_out, bit_extender_2_out;

  assign bit_extender_1_out = {{16{1'b0}}, _16bit_Input};  // Bit_Extender bit_extender_1
  assign bit_extender_2_out = {{16{_16bit_Input[15]}}, _16bit_Input};  // Bit_Extender bit_extender_2
  Multiplexer #(.width(32)) multiplexer_1 (
    .in0(bit_extender_1_out), .in1(bit_extender_2_out), .out(Output), .sel(Select));  // open: en
endmodule

module PC_Controller (
  input  Zero,
  input  PCCtrl1,
  input  PCCtrl0,
  output PCSrc1,
  output PCSrc0
);

  wire and_1_out, and_3_out;

  and and_1 (and_1_out, Zero, PCCtrl1, ~PCCtrl0);  // AND_Gate
  and and_2 (PCSrc0, PCCtrl1, PCCtrl0);
  and and_3 (and_3_out, ~Zero, ~PCCtrl1, PCCtrl0);  // AND_Gate
  or or_1 (PCSrc1, and_1_out, and_3_out);

  // Notes on the sheet:
  //   Rest => PCCtrl1 = 0, PCCtrl1 = 0
  //   BNE => PCCtrl1 = 0, PCCtrl0 = 1
  //   BEQ => PCCtrl1 = 1, PCCtrl0 = 0 
  //   Jump => PCCtrl1 = 1, PCCtrl0 = 1
  //   PCSrc is computed using slide 59 from Chapter 4.1-4.4
  //   PCCtrl0 and PCCtrl1 are coming from Main Control
  //   Zero should come from Zero Flag in ALU
endmodule

module ALU_Control (
  input  [3:0] ALU_Control_Input,
  input  ALUOp2,
  input  ALUOp1,
  input  ALUOp0,
  output [2:0] ALU_Opcode
);

  wire and_1_out, and_2_out, and_3_out, and_4_out, and_5_out, and_6_out, or_4_out;
  wire [2:0] or_1_out;

  and and_1 (and_1_out, ~ALU_Control_Input[3], ALU_Control_Input[2], ~ALU_Control_Input[1], ~ALU_Control_Input[0]);  // AND_Gate
  and and_2 (and_2_out, ~ALU_Control_Input[3], ALU_Control_Input[2], ALU_Control_Input[1], ~ALU_Control_Input[0]);  // AND_Gate
  and and_3 (and_3_out, ~ALU_Control_Input[3], ~ALU_Control_Input[2], ALU_Control_Input[1], ~ALU_Control_Input[0]);  // AND_Gate
  and and_4 (and_4_out, ~ALU_Control_Input[3], ~ALU_Control_Input[2], ~ALU_Control_Input[1], ~ALU_Control_Input[0]);  // AND_Gate
  and and_5 (and_5_out, ALU_Control_Input[3], ~ALU_Control_Input[2], ALU_Control_Input[1], ~ALU_Control_Input[0]);  // AND_Gate
  and and_6 (and_6_out, ~ALU_Control_Input[3], ALU_Control_Input[2], ~ALU_Control_Input[1], ALU_Control_Input[0]);  // AND_Gate
  or or_1 (or_1_out[0], and_1_out, and_2_out, and_3_out);
  or or_2 (or_1_out[1], and_2_out, and_6_out, and_5_out);
  or or_3 (or_1_out[2], and_3_out, and_4_out, and_5_out);
  or or_4 (or_4_out, ALUOp2, ALUOp1, ALUOp0);
  Multiplexer #(.width(3)) multiplexer_1 (
    .in0(or_1_out), .in1({ALUOp2, ALUOp1, ALUOp0}), .out(ALU_Opcode), .sel(or_4_out));  // open: en
endmodule
